// Logisim project circuits.circ as structural Verilog: 6 circuits, main circuit main
module main (
  output [7:0] out_1,
  output [7:0] out_2
);

  AddMachine addmachine_1 (.out_1(out_2), .out_2(out_1));
endmodule

module NAND (
  input  in_1,
  input  in_2,
  output out_3
);

  wire and_1_out;

  and and_1 (and_1_out, in_1, in_2);
  not not_1 (out_3, and_1_out);
endmodule

module XOR (
  input  in_1,
  input  in_2,
  output out_3
);

  wire and_1_out, not_1_out, or_1_out;

  or or_1 (or_1_out, in_1, in_2);
  and and_1 (and_1_out, in_1, in_2);
  not not_1 (not_1_out, and_1_out);
  and and_2 (out_3, or_1_out, not_1_out);
endmodule

module _2_to_1_MUX (
  input  A,
  input  SEL,
  input  B,
  output out_4
);

  wire and_1_out, and_2_out, not_1_out;

  not not_1 (not_1_out, SEL);
  and and_1 (and_1_out, not_1_out, A);
  and and_2 (and_2_out, SEL, B);
  or or_1 (out_4, and_1_out, and_2_out);
endmodule

module _4_to_1_MUX (
  input  A,
  input  SEL_1,
  input  B,
  input  C,
  input  SEL_2,
  input  D,
  output out_7
);

  wire and_1_out, and_2_out, and_3_out, and_4_out, not_1_out, not_2_out;

  not not_1 (not_1_out, SEL_1);
  not not_2 (not_2_out, SEL_2);
  and and_1 (and_1_out, not_1_out, B, SEL_2);
  and and_2 (and_2_out, not_2_out, SEL_1, C);
  and and_3 (and_3_out, SEL_2, SEL_1, D);
  and and_4 (and_4_out, not_1_out, A, not_2_out);
  or or_1 (out_7, and_4_out, and_1_out, and_2_out, and_3_out);
endmodule

module AddMachine (
  output [7:0] out_1,
  output [7:0] out_2
);

  wire clock_1_out;

  Adder adder_1 (.a(8'h1), .b(out_2), .out(out_1));  // open: cin, cout
  Clock clock_1 (.out(clock_1_out));
  Register register_1 (.D(out_1), .Q(out_2), .clk(clock_1_out));  // open: en, clr
endmodule
