// Logisim project partA.circ as structural Verilog
module Ex1 (
  input  [7:0] in_1,
  input  in_2,
  output Out1,
  output [7:0] out_4
);

  and and_1 (Out1, in_1[0], in_1[7]);

  assign out_4 = {in_2, in_1[6:0]};

  // Notes on the sheet:
  //   8 Bit Input
  //   Out2
endmodule

module shiftOne (
  input  [15:0] in_1,
  output [15:0] out_2
);


  assign out_2 = {in_1[0], in_1[15:1]};

  // Other names for the same wires on the sheet: input[15:0] = in_1
endmodule

module shiftTwo (
  input  [15:0] in_1,
  output [15:0] out_2
);


  assign out_2 = {in_1[1:0], in_1[15:2]};

  // Other names for the same wires on the sheet: input[15:0] = in_1
endmodule

module shiftFour (
  input  [15:0] in_1,
  output [15:0] out_2
);


  assign out_2 = {in_1[3:0], in_1[15:4]};

  // Other names for the same wires on the sheet: input[15:0] = in_1
endmodule

module shiftEight (
  input  [15:0] in_1,
  output [15:0] out_2
);


  assign out_2 = {in_1[7:0], in_1[15:8]};

  // Other names for the same wires on the sheet: input[15:0] = in_1
endmodule

module shiftThree (
  input  [15:0] in_1,
  output [15:0] out_2
);


  assign out_2 = {in_1[15:3], 3'b000};

  // Other names for the same wires on the sheet: input[15:0] = in_1
endmodule
